# Fritzing sketch smart-power-meter (saved by Fritzing 0.9.10b)

parts:
  Orange_Pi_One1 = Orange Pi One [part_number=OPI-ONE]
  KY-1 = Keyes Relay [package=THT]
  Display1 = LCD screen 16x2 IIC [part_number=101290]
  MAX471_Current_and_Voltage_Sensor1 = MAX471 Current and Voltage Sensor Module
  LED1 = smd LED [color="Red (633nm)" package="0805 [SMD]"]
  VCC1 = Battery block 9V

nets:
  N1: Orange_Pi_One1.PA12, Display1.SDA
  N2: Orange_Pi_One1.PA11, Display1.SCL
  GND: Orange_Pi_One1.GND, KY-1.ground, Display1.GND, MAX471_Current_and_Voltage_Sensor1.GND#12, MAX471_Current_and_Voltage_Sensor1.GND#13
  N3: Orange_Pi_One1.PA1, MAX471_Current_and_Voltage_Sensor1.AT
  N4: Orange_Pi_One1.PA0, MAX471_Current_and_Voltage_Sensor1.VT
  N5: Orange_Pi_One1.PA3, KY-1.signal
  5V: Orange_Pi_One1.5V, KY-1.power, Display1.VCC
  N6: KY-1.C, VCC1.+
  N7: KY-1.NO, MAX471_Current_and_Voltage_Sensor1.VIN
  N8: MAX471_Current_and_Voltage_Sensor1.GND#8, LED1.cathode
  N9: MAX471_Current_and_Voltage_Sensor1.VOUT, LED1.anode
  N10: MAX471_Current_and_Voltage_Sensor1.GND#10, VCC1.-

custom parts:
  Orange Pi One: It’s an open-source single-board computer. It can run Android 4.4, Ubuntu, Debian, Rasberry Pi Image, as well as the banana pi Image. It uses the AllWinner H3 SoC, and has 512MB DDR3 SDRAM
  Keyes Relay: The Keyes 5V relay module is suitable for SCM development, home appliance control. It uses a 5V~12V TIL control signal which can control DC / AC signal.
  LCD screen 16x2 IIC: LCD screen with HD44780 controller enables showing text, symbols, value or anything else that comes from Croduino/Arduino. It is capable of showing 16 symbols in two lines and therefore can be used in many projects that need to send clearly visible and legible output information.. • Color of symbols: White • Backlight: Blue • Dimensions: 80 x 36 x 12 mm • Screen dimensions: 64.5 x 16 mm •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
  MAX471 Current and Voltage Sensor Module: The MAX471 current and voltage sensor module is a bidirectional, highside current-sense amplifier. The current measurement maximum is 3 amps and the voltage measurement range is 3 to 25 volts. The operating voltage range is 3 to 36 volts.
